// Logisim project angulaire.circ as structural Verilog: 7 circuits, main circuit angulaire_controller
module leds (
  input  CHA,
  input  CHB,
  input  CHC,
  input  RESET,
  output [9:0] leds_ouput,
  output VDD,
  output GND
);

  wire [3:0] angulaire_controller_1_state;

  angulaire_controller angulaire_controller_1 (
    .CHA(CHA), .CHB(CHB), .CHC(CHC), .reset(RESET), .state(angulaire_controller_1_state), .VDD(VDD), .GND(GND));  // open: Selected
  encode_4_leds encode_4_leds_1 (.A(angulaire_controller_1_state), .leds(leds_ouput));
endmodule

module sevenseg (
  input  CHA,
  input  CHB,
  input  CHC,
  input  RESET,
  output VDD,
  output GND
);

  wire clock_1_out, en_cnt, t_ff_1_q;
  wire [3:0] angulaire_controller_1_state;
  wire [6:0] seven_seg_encodeur_1_seg;

  T_Flip_Flop t_ff_1 (.T(en_cnt), .clk(clock_1_out), .Q(t_ff_1_q));  // open: Qn, reset, preset
  Clock clock_1 (.out(clock_1_out));
  Counter counter_1 (.clk(t_ff_1_q));  // open: clr, load, up, count, D, carry, Q
  angulaire_controller angulaire_controller_1 (
    .CHA(CHA), .CHB(CHB), .CHC(CHC), .reset(RESET), .state(angulaire_controller_1_state), .VDD(VDD), .GND(GND));  // open: Selected
  seven_seg_encodeur seven_seg_encodeur_1 (.A(angulaire_controller_1_state), .seg(seven_seg_encodeur_1_seg));
  _7_Segment_Display L_7_Segment_Display_1 (
    .g(seven_seg_encodeur_1_seg[6]), .f(seven_seg_encodeur_1_seg[5]), .a(seven_seg_encodeur_1_seg[0]),
    .b(seven_seg_encodeur_1_seg[1]), .e(seven_seg_encodeur_1_seg[4]), .d(seven_seg_encodeur_1_seg[3]),
    .c(seven_seg_encodeur_1_seg[2]));  // open: dp
endmodule

module angulaire_controller (
  input  CHA,
  input  CHB,
  input  CHC,
  input  reset,
  output Selected,
  output [3:0] state,
  output VDD,
  output GND
);

  wire and_1_out, clock_1_out, comparator_1_eq, comparator_2_eq, d_ff_1_q, d_ff_2_q, d_ff_3_q, d_ff_4_q,
       d_ff_5_q, debounce_1_filtered, debounce_2_filtered, dir, en_cnt, or_1_out, or_2_out, t_ff_1_q;

  Clock clock_1 (.out(clock_1_out));
  or or_1 (or_1_out, reset, comparator_1_eq);
  debounce debounce_1 (.raw(CHA), .clck(clock_1_out), .filtered(debounce_1_filtered));
  debounce debounce_2 (.raw(CHB), .clck(clock_1_out), .filtered(debounce_2_filtered));
  debounce debounce_3 (.raw(CHC), .clck(clock_1_out), .filtered(Selected));
  T_Flip_Flop t_ff_1 (.T(en_cnt), .clk(clock_1_out), .Q(t_ff_1_q));  // open: Qn, reset, preset
  D_Flip_Flop d_ff_1 (.D(dir), .clk(clock_1_out), .Q(d_ff_1_q));  // open: Qn, preset, reset
  D_Flip_Flop d_ff_2 (.D(debounce_1_filtered), .clk(clock_1_out), .Q(d_ff_2_q));  // open: Qn, preset, reset
  D_Flip_Flop d_ff_3 (.D(debounce_2_filtered), .clk(clock_1_out), .Q(d_ff_3_q));  // open: Qn, preset, reset
  Counter #(.max('hf), .width(4)) counter_1 (
    .clr(or_1_out), .load(comparator_2_eq), .up(d_ff_1_q), .count(1'b1), .clk(or_2_out), .D(4'b1001),
    .Q(state));  // open: carry
  or or_2 (or_2_out, t_ff_1_q, and_1_out);
  D_Flip_Flop d_ff_4 (.D(comparator_2_eq), .clk(clock_1_out), .Q(d_ff_4_q));  // open: Qn, preset, reset
  D_Flip_Flop d_ff_5 (.D(t_ff_1_q), .clk(clock_1_out), .Q(d_ff_5_q));  // open: Qn, preset, reset
  Comparator #(.mode("unsigned"), .width(4)) comparator_1 (
    .a(state), .b(4'b1010), .eq(comparator_1_eq));  // open: gt, lt
  Comparator #(.mode("unsigned"), .width(4)) comparator_2 (
    .a(state), .b(4'b1111), .eq(comparator_2_eq));  // open: gt, lt
  and and_1 (and_1_out, d_ff_4_q, ~d_ff_5_q);  // AND_Gate
  decodeur decodeur_1 (
    .Bp(d_ff_3_q), .Ap(d_ff_2_q), .Bc(debounce_2_filtered), .Ac(debounce_1_filtered), .dir(dir),
    .en_cnt(en_cnt));

  assign GND = 1'b0;
  assign VDD = 1'b1;
endmodule

module debounce (
  input  raw,
  input  clck,
  output filtered
);

  wire and_1_out, and_2_out, d_ff_1_q, d_ff_2_q, d_ff_3_q, d_ff_4_q;

  D_Flip_Flop d_ff_1 (.D(raw), .clk(clck), .Q(d_ff_1_q));  // open: Qn, preset, reset
  D_Flip_Flop d_ff_2 (.D(d_ff_1_q), .clk(clck), .Q(d_ff_2_q));  // open: Qn, preset, reset
  D_Flip_Flop d_ff_3 (.D(d_ff_2_q), .clk(clck), .Q(d_ff_3_q));  // open: Qn, preset, reset
  D_Flip_Flop d_ff_4 (.D(d_ff_3_q), .clk(clck), .Q(d_ff_4_q));  // open: Qn, preset, reset
  and and_1 (and_1_out, d_ff_2_q, d_ff_3_q, d_ff_4_q);
  and and_2 (and_2_out, ~d_ff_4_q, ~d_ff_3_q, ~d_ff_2_q);  // AND_Gate
  J_K_Flip_Flop j_k_ff_1 (.J(and_1_out), .K(and_2_out), .clk(clck), .Q(filtered));  // open: Qn, preset, reset
endmodule

module decodeur (
  input  Bp,
  input  Ap,
  input  Bc,
  input  Ac,
  output dir,
  output en_cnt
);

  wire and_1_out, and_2_out, and_3_out, and_4_out, and_5_out, and_6_out, not_1_out, not_2_out, not_3_out,
       not_4_out;

  not not_1 (not_1_out, Bp);
  not not_2 (not_2_out, Ap);
  not not_3 (not_3_out, Bc);
  not not_4 (not_4_out, Ac);
  and and_1 (and_1_out, not_2_out, not_3_out);
  and and_2 (and_2_out, Ap, Bc);
  and and_3 (and_3_out, not_2_out, Ac);
  and and_4 (and_4_out, not_1_out, Bc);
  and and_5 (and_5_out, Ap, not_4_out);
  and and_6 (and_6_out, Bp, not_3_out);
  or or_1 (dir, and_1_out, and_2_out);
  or or_2 (en_cnt, and_3_out, and_4_out, and_5_out, and_6_out);
endmodule

module seven_seg_encodeur (
  input  [3:0] A,
  output [6:0] seg
);

  wire and_1_out, and_2_out, and_3_out, and_4_out, and_5_out, and_6_out, and_7_out, and_8_out, and_9_out,
       and_10_out, and_11_out, and_12_out, and_13_out, and_14_out, and_15_out, and_16_out, not_1_out,
       not_2_out, not_3_out;

  not not_1 (not_1_out, A[2]);
  not not_2 (not_2_out, A[1]);
  not not_3 (not_3_out, A[0]);
  and and_1 (and_1_out, not_1_out, A[1]);
  and and_2 (and_2_out, A[2], not_2_out);
  and and_3 (and_3_out, A[2], not_3_out);
  and and_4 (and_4_out, not_2_out, not_3_out);
  and and_5 (and_5_out, A[2], not_2_out);
  and and_6 (and_6_out, A[2], not_3_out);
  and and_7 (and_7_out, not_1_out, not_3_out);
  or or_1 (seg[4], and_7_out, and_8_out);
  and and_8 (and_8_out, A[1], not_3_out);
  and and_9 (and_9_out, not_1_out, not_3_out);
  and and_10 (and_10_out, not_1_out, A[1]);
  and and_11 (and_11_out, A[1], not_3_out);
  and and_12 (and_12_out, A[2], not_2_out, A[0]);
  or or_2 (seg[2], not_2_out, A[0], A[2]);
  and and_13 (and_13_out, not_2_out, not_3_out);
  or or_3 (seg[1], not_1_out, and_13_out, and_14_out);
  and and_14 (and_14_out, A[1], A[0]);
  and and_15 (and_15_out, not_1_out, not_3_out);
  and and_16 (and_16_out, A[2], A[0]);
  or or_4 (seg[6], and_1_out, and_2_out, and_3_out, A[3]);
  or or_5 (seg[5], and_4_out, and_5_out, and_6_out, A[3]);
  or or_6 (seg[3], and_9_out, and_10_out, and_11_out, and_12_out);
  or or_7 (seg[0], and_15_out, A[1], and_16_out, A[3]);
endmodule

module encode_4_leds (
  input  [3:0] A,
  output [9:0] leds
);

  wire not_1_out, not_2_out, not_3_out, not_4_out;

  not not_1 (not_1_out, A[3]);
  not not_2 (not_2_out, A[2]);
  not not_3 (not_3_out, A[1]);
  not not_4 (not_4_out, A[0]);
  and and_1 (leds[9], A[3], not_2_out, not_3_out, A[0]);
  and and_2 (leds[8], A[3], not_2_out, not_3_out, not_4_out);
  and and_3 (leds[7], not_1_out, A[2], A[1], A[0]);
  and and_4 (leds[6], not_1_out, A[2], A[1], not_4_out);
  and and_5 (leds[5], not_1_out, A[2], not_3_out, A[0]);
  and and_6 (leds[4], not_1_out, A[2], not_3_out, not_4_out);
  and and_7 (leds[3], not_1_out, not_2_out, A[1], A[0]);
  and and_8 (leds[2], not_1_out, not_2_out, A[1], not_4_out);
  and and_9 (leds[1], not_1_out, not_2_out, not_3_out, A[0]);
  and and_10 (leds[0], not_1_out, not_2_out, not_3_out, not_4_out);
endmodule
